// Logisim project mainCPU.circ as structural Verilog: 1 circuit, main circuit main
module main (
  input  [7:0] in_1,
  input  [7:0] in_2,
  input  [1:0] in_3,
  input  in_4,
  input  in_5,
  input  in_6,
  input  in_7,
  input  [7:0] in_8,
  output [7:0] out_9,
  output [7:0] out_10,
  output [7:0] out_11,
  output [7:0] out_12,
  output [7:0] out_13
);

  wire and_1_out, and_2_out, clock_1_out, not_1_out, or_1_out, xor_1_out;
  wire [7:0] demultiplexer_1_out1, demultiplexer_1_out3, demultiplexer_1_out4, demultiplexer_1_out5,
       multiplexer_1_out, multiplexer_2_out, multiplexer_4_out, multiplexer_5_out, ram_1_data, register_1_q,
       register_2_q, register_3_q, rom_1_data;

  Demultiplexer #(.select(3), .width(8)) demultiplexer_1 (
    .out1(demultiplexer_1_out1), .out3(demultiplexer_1_out3), .out4(demultiplexer_1_out4),
    .out5(demultiplexer_1_out5), .in(in_2), .sel({in_6, in_5, in_4}));  // open: out0, out2, out6, out7, en
  Demultiplexer #(.select(3), .width(8)) demultiplexer_2 (
    .out1(out_11), .out2(out_12), .out3(out_13), .in(in_8), .sel({in_6, in_5, in_4}));  // open: out0, out4, out5, out6, out7, en
  Multiplexer #(.width(8)) multiplexer_1 (
    .in0(demultiplexer_1_out1), .in1(demultiplexer_1_out4), .out(multiplexer_1_out), .sel(in_6));  // open: en
  Multiplexer #(.width(8)) multiplexer_2 (
    .in0(demultiplexer_1_out3), .in1(demultiplexer_1_out5), .out(multiplexer_2_out), .sel(in_6));  // open: en
  Multiplexer #(.select(2), .width(8)) multiplexer_3 (
    .in1(out_11), .in2(out_12), .in3(out_13), .out(out_10), .sel({in_6, in_5}));  // open: in0, en
  not not_1 (not_1_out, in_6);
  or or_1 (or_1_out, in_4, in_5);
  xor xor_1 (xor_1_out, in_4, in_5);
  ROM rom_1 (.addr(multiplexer_1_out), .data(rom_1_data));  // open: sel
  Multiplexer #(.width(8)) multiplexer_4 (
    .in0(multiplexer_2_out), .in1(out_10), .out(multiplexer_4_out), .sel(in_7));  // open: en
  and and_1 (and_1_out, not_1_out, or_1_out);
  and and_2 (and_2_out, in_6, xor_1_out);
  Clock clock_1 (.out(clock_1_out));
  RAM #(.bus("separate")) ram_1 (
    .addr(multiplexer_4_out), .din(out_9), .data(ram_1_data), .str(and_1_out), .clk(clock_1_out),
    .ld(and_2_out));  // open: sel, clr
  Multiplexer #(.select(2), .width(8)) multiplexer_5 (
    .in1(ram_1_data), .in2(rom_1_data), .in3(in_1), .out(multiplexer_5_out), .sel(in_3));  // open: in0, en
  Register register_1 (.D(multiplexer_5_out), .Q(register_1_q), .clk(clock_1_out));  // open: en, clr
  Register register_2 (.D(register_1_q), .Q(register_2_q), .clk(clock_1_out));  // open: en, clr
  Register register_3 (.D(register_2_q), .Q(register_3_q), .clk(clock_1_out));  // open: en, clr
  Register register_4 (.D(register_3_q), .clk(clock_1_out));  // open: en, Q, clr
endmodule
